# Fritzing sketch Circuito proyecto FBIO (saved by Fritzing 0.9.4)

parts:
  Componente2 = Arduino Nano (Rev3.0) (ICSP)
  MPX1 = MPX2010 pressure sensor [part_number=MPX]
  Componente3 = Bluetooth HC-05 Macho
  U1 = LIPO-110mAh [package=lipo-110]
  M2 = TP4056 Module [part_number=HW-107]
  J1 = Camdenboss CTB0158-3 [part_number=CTB0158-3 package=THT]

nets:
  N1: Componente2.D1/TX, Componente3.RXD
  N2: Componente2.D0/RX, Componente3.TXD
  GND: Componente2.GND, MPX1.GND, Componente3.GND, M2.OUT-#1, J1.pin2
  N3: Componente2.VIN, J1.pin3
  5V: Componente2.5V, MPX1.Vs, Componente3.VCC
  N4: Componente2.A2, MPX1.V_out_+
  N5: Componente2.A1, MPX1.V_out_-
  N6: U1.+, M2.BAT+
  N7: U1.-, M2.BAT-
  N8: M2.OUT-#4, J1.pin1

custom parts:
  TP4056 Module: TP4056 Lithium Battery Charge Management Module Links: TP4056 website
